# Fritzing sketch phteven-cjmcu-8223 smd (saved by Fritzing 0.9.3b)
circuit board: 2.5cm x 4.8cm
breadboards: 1

parts:
  J1 = female pin header, 10 pins [form="♀ (female)"]
  J2 = female pin header, 10 pins [form="♀ (female)"]
  J3 = female pin header, 5 pins [form="♀ (female)"]
  R2 = Resistor [tolerance=±5% resistance=22k package=THT]
  R1 = Resistor [tolerance=±5% resistance=33k package=THT]
  UI_BOTTOM = Header 8 [package=1x08_smd]
  UI_TOP = Header 8 [package=1x08_smd]
  Pad9 = Pad [width=1.27 height=5.5 connect=center]
  Pad10 = Pad [width=1.27 height=5.5 connect=center]
  Pad11 = Pad [width=1.27 height=5.5 connect=center]
  Pad12 = Pad [width=1.27 height=5.5 connect=center]
  Pad13 = Pad [width=1.27 height=5.5 connect=center]
  Pad14 = Pad [width=1.27 height=5.5 connect=center]
  Pad15 = Pad [width=1.27 height=5.5 connect=center]
  Pad16 = Pad [width=1.27 height=5.5 connect=center]
  Pad17 = Pad [width=1.27 height=5.5 connect=center]
  Pad18 = Pad [width=1.27 height=5.5 connect=center]
  Pad19 = Pad [width=1.27 height=5.5 connect=center]
  Pad20 = Pad [width=1.27 height=5.5 connect=center]
  Pad21 = Pad [width=1.27 height=5.5 connect=center]
  Pad22 = Pad [width=1.27 height=5.5 connect=center]
  Pad23 = Pad [width=1.27 height=5.5 connect=center]
  Pad24 = Pad [width=1.27 height=3 connect=center]
  J4 = male pin header, 2 pins [form="♂ (male)"]

nets:
  GND/PWSW+: J1.pin1, J1.pin10, J2.pin10, J3.pin1, R1.Pin_1, UI_BOTTOM.1, UI_BOTTOM.7, UI_TOP.1, Pad17.pad, Pad23.pad, Pad24.pad
  3V3: J1.pin2, J2.pin9, J3.pin5, UI_TOP.8, Pad12.pad
  P23: J1.pin3, R2.Pin_0
  P24: J1.pin4
  P25: J1.pin5, UI_TOP.7, Pad20.pad
  P28: J1.pin6, UI_TOP.6, Pad11.pad
  P29: J1.pin7, UI_TOP.5, Pad19.pad
  P30: J1.pin8, UI_TOP.4, Pad10.pad
  P00: J1.pin9, UI_TOP.3, Pad18.pad
  SWCLK: J2.pin1, J4.pin2
  SWDIO: J2.pin2, J4.pin1
  P16: J2.pin3, UI_BOTTOM.6, Pad13.pad
  P15: J2.pin4, UI_BOTTOM.5, Pad22.pad
  P12: J2.pin5, UI_BOTTOM.4, Pad14.pad
  P11: J2.pin6, UI_BOTTOM.3, Pad21.pad
  P09: J2.pin7, UI_BOTTOM.2, Pad15.pad
  P08: J2.pin8
  CRG+: J3.pin2, UI_TOP.2, Pad9.pad
  BAT_OUT: J3.pin3, R2.Pin_1, R1.Pin_0
  BAT_SW/PWSW-: J3.pin4, UI_BOTTOM.8, Pad16.pad
