# Fritzing sketch phteven_adafruit_nrf52 pth (saved by Fritzing 0.9.3b)
circuit board: 2.4cm x 4.2cm
breadboards: 1

parts:
  J1 = female pin header, 16 pins [form="♀ (female)"]
  J2 = female pin header, 12 pins [form="♀ (female)"]
  J4 = double row female pin header, 12 pins [form="♀ (female)"]
  J5 = female pin header, 3 pins [form="♀ (female)"]
  R1 = Resistor [tolerance=±5% resistance=0 package=THT]
  R5 = Resistor [tolerance=±5% resistance=0 package=THT]
  R4 = Resistor [tolerance=±5% resistance=0 package=THT]
  R3 = Resistor [tolerance=±5% resistance=10k package=THT]
  R2 = Resistor [tolerance=±5% resistance=10k package=THT]
  J6 = female pin header, 4 pins [form="♀ (female)"]

nets:
  EN 3V3/Reset / 35: J1.pin1, J2.pin2, J5.pin3
  3V3: J1.pin2, J1.pin3, R1.Pin_0, R4.Pin_1, R3.Pin_1, R2.Pin_1
  GND: J1.pin4, J4.pin6, J5.pin1, R5.Pin_1
  A0 / 2: J1.pin5
  A1 / 3: J1.pin6, J4.pin8
  A2 / 4: J1.pin7, J4.pin9
  A3 / 5: J1.pin8, J4.pin10
  A4 / 28: J1.pin9, J4.pin11
  A5 / 29: J1.pin10, J4.pin12
  12 (SCK): J1.pin11, J4.pin1
  13 (MOSI): J1.pin12, J4.pin2
  14 (MISO): J1.pin13, J4.pin3
  8 (RX): J1.pin14
  6 (TX): J1.pin15
  20 (DFU): J1.pin16
  VBAT: J2.pin1
  VBUS: J2.pin3, J5.pin2
  16: J2.pin4
  15: J2.pin5
  7: J2.pin6
  11: J2.pin7
  A7 / 31 (VBAT Level): J2.pin8
  A6 / 30: J2.pin9, J4.pin5
  27: J2.pin10, J4.pin4
  26 (SCL): J2.pin11
  25 (SDA): J2.pin12
  N1: J4.pin7, R1.Pin_1
  N2: R5.Pin_0, J6.pin4
  N3: R4.Pin_0, J6.pin3
  N4: R3.Pin_0, J6.pin2
  N5: R2.Pin_0, J6.pin1
