# Fritzing sketch phteven_adafruit_nrf52 smd (saved by Fritzing 0.9.3b)
circuit board: 2.4cm x 5cm
breadboards: 1

parts:
  J1 = female pin header, 16 pins [form="♀ (female)"]
  J2 = female pin header, 12 pins [form="♀ (female)"]
  UI_TOP = Header 8 [package=1x08_smd]
  UI_BOTTOM = Header 8 [package=1x08_smd]
  R1 = Resistor [tolerance=±5% resistance=10k package=THT]
  R2 = Resistor [tolerance=±5% resistance=10k package=THT]
  I2C = female pin header, 4 pins [form="♀ (female)"]
  Pad1 = Pad [width=1.27 height=4.5 connect=center]
  Pad2 = Pad [width=1.27 height=4.5 connect=center]
  Pad3 = Pad [width=1.27 height=4.5 connect=center]
  Pad4 = Pad [width=1.27 height=4.5 connect=center]
  Pad5 = Pad [width=1.27 height=4.5 connect=center]
  Pad6 = Pad [width=1.27 height=4.5 connect=center]
  Pad7 = Pad [width=1.27 height=4.5 connect=center]
  Pad8 = Pad [width=1.27 height=4.5 connect=center]
  Pad9 = Pad [width=1.27 height=4.5 connect=center]
  Pad10 = Pad [width=1.27 height=4.5 connect=center]
  Pad11 = Pad [width=1.27 height=4.5 connect=center]
  Pad12 = Pad [width=1.27 height=4.5 connect=center]
  Pad13 = Pad [width=1.27 height=4.5 connect=center]
  Pad14 = Pad [width=1.27 height=4.5 connect=center]
  Pad15 = Pad [width=1.27 height=4.5 connect=center]
  Pad16 = Pad [width=1.27 height=4.5 connect=center]
  BAT = Header 2 [package=jst-2-pth]

nets:
  Reset / 35: J1.pin1
  3V3: J1.pin2, J1.pin3, UI_TOP.8, R1.Pin_1, R2.Pin_1, I2C.pin3, Pad8.pad
  GND/PWSW-: J1.pin4, UI_BOTTOM.1, UI_BOTTOM.7, UI_BOTTOM.8, I2C.pin4, Pad9.pad, Pad15.pad, Pad16.pad, BAT.1
  A0 / 2: J1.pin5, UI_BOTTOM.2, Pad10.pad
  A1 / 3: J1.pin6, UI_BOTTOM.3, Pad11.pad
  A2 / 4: J1.pin7, UI_BOTTOM.4, Pad12.pad
  A3 / 5: J1.pin8, UI_BOTTOM.5, Pad13.pad
  A4 / 28: J1.pin9, UI_BOTTOM.6, Pad14.pad
  A5 / 29: J1.pin10
  12 (SCK): J1.pin11
  13 (MOSI): J1.pin12
  14 (MISO): J1.pin13
  8 (RX): J1.pin14
  6 (TX): J1.pin15
  20 (DFU): J1.pin16
  VBAT: J2.pin1, BAT.2
  EN 3V3/PWSW+: J2.pin2, UI_TOP.1, Pad1.pad
  CHG+/VBUS: J2.pin3, UI_TOP.2, Pad2.pad
  16: J2.pin4, UI_TOP.3, Pad3.pad
  15: J2.pin5, UI_TOP.4, Pad4.pad
  7: J2.pin6, UI_TOP.5, Pad5.pad
  11: J2.pin7, UI_TOP.6, Pad6.pad
  A7 / 31 (VBAT Level): J2.pin8
  A6 / 30: J2.pin9, UI_TOP.7, Pad7.pad
  27: J2.pin10
  26 (SCL)/I2C SCL: J2.pin11, R1.Pin_0, I2C.pin2
  25 (SDA)/I2C SDA: J2.pin12, R2.Pin_0, I2C.pin1

notes:
  T
  B
