# Fritzing sketch tp4056 charger carrier (saved by Fritzing 0.9.3b)
circuit board: 2cm x 3.4cm
breadboards: 1

parts:
  BAT+ = male pin header, 1 pin [form="♂ (male)"]
  BAT- = male pin header, 1 pin [form="♂ (male)"]
  IN- = male pin header, 1 pin [form="♂ (male)"]
  IC1 = Voltage Regulator [package=to-92]
  C1 = Tantalum Capacitor [capacitance=2.2µF package="100 mil [THT, tantalum]"]
  BAT_OUT = male pin header, 1 pin [form="♂ (male)"]
  3V3_OUT = female pin header, 1 pin [form="♀ (female)"]
  BAT_SW = female pin header, 1 pin [form="♀ (female)"]  # not connected
  IN+ = male pin header, 1 pin [form="♂ (male)"]
  IN_CON = female pin header, 1 pin [form="♀ (female)"]
  GND = female pin header, 1 pin [form="♀ (female)"]  # not connected

nets:
  N1: BAT+.pin1, IC1.IN, BAT_OUT.pin1
  GND: BAT-.pin1, IN-.pin1, C1.-
  N2: IC1.OUT, C1.+, 3V3_OUT.pin1
  N3: IN+.pin1, IN_CON.pin1

custom parts:
  Voltage Regulator: Voltage Regulator Standard L4931 regulator]
